// Logisim project this.circ as structural Verilog: 7 circuits, main circuit main
module main (
  input  [15:0] in_1,
  input  in_2
);

  wire clock_1_out, clock_2_out, controlled_buffer_1_out, cpu_1_conditional, not_1_out, not_2_out,
       rgb_video_1_p3, tpu_1_clockou;
  wire [4:0] rgb_video_1_p5, rgb_video_1_p6;
  wire [6:0] tpu_1_out_3;
  wire [15:0] controlled_buffer_3_out, counter_1_q, cpu_1_display, cpu_1_ou, cpu_1_text, rgb_video_1_p7,
       rom_1_data, rom_2_data, rom_3_data, rom_4_data;

  Clock clock_1 (.out(clock_1_out));
  not not_1 (not_1_out, clock_1_out);
  assign controlled_buffer_1_out = not_2_out ? clock_1_out : 1'bz;  // Controlled_Buffer controlled_buffer_1
  assign controlled_buffer_1_out = cpu_1_conditional ? not_1_out : 1'bz;  // Controlled_Buffer controlled_buffer_2
  not not_2 (not_2_out, cpu_1_conditional);
  Counter #(.max('hffff), .width(16)) counter_1 (
    .clr(in_2), .load(cpu_1_conditional), .up(1'b1), .clk(controlled_buffer_1_out),
    .D(controlled_buffer_3_out), .Q(counter_1_q));  // open: count, carry
  ROM #(.addrWidth(16), .dataWidth(16)) rom_1 (.addr(counter_1_q), .data(rom_1_data));
  ROM #(.addrWidth(16), .dataWidth(16)) rom_2 (.addr(counter_1_q), .data(rom_2_data));
  ROM #(.addrWidth(16), .dataWidth(16)) rom_3 (.addr(counter_1_q), .data(rom_3_data));
  ROM #(.addrWidth(16), .dataWidth(16)) rom_4 (.addr(counter_1_q), .data(rom_4_data));
  assign controlled_buffer_3_out = cpu_1_conditional ? rom_4_data : 16'bz;  // Controlled_Buffer controlled_buffer_3
  CPU cpu_1 (
    .OPCode(rom_1_data), .C1(rom_2_data), .C2(rom_3_data), .C3(rom_4_data), .IP(in_1), .Reset(in_2),
    .OU(cpu_1_ou), .Conditional(cpu_1_conditional), .Display(cpu_1_display), .Text(cpu_1_text));
  // RGB_Video #(.height(32), .scale(7), .width(32)) rgb_video_1: pin names not known; wires that end beside it: cpu_1_ou, in_2, rgb_video_1_p3, rgb_video_1_p3, rgb_video_1_p5, rgb_video_1_p6, rgb_video_1_p7
  GPU gpu_1 (
    .Reset(in_2), .Clock(clock_2_out), .Color(cpu_1_display), .ClockOU(rgb_video_1_p3), .X(rgb_video_1_p5),
    .Y(rgb_video_1_p6), .Colorr(rgb_video_1_p7));
  Clock clock_2 (.out(clock_2_out));
  TTY tty_1 (.data(tpu_1_out_3), .clk(tpu_1_clockou), .we(tpu_1_clockou), .clr(in_2));
  TPU tpu_1 (.Char(cpu_1_text), .Clock(clock_2_out), .out_3(tpu_1_out_3), .ClockOU(tpu_1_clockou));

  // Notes on the sheet:
  //   contents of rom_1 (hex, n*v repeats v):
  //   0 0 18 2 2 1b 0 2 2 1b
  //   contents of rom_2 (hex, n*v repeats v):
  //   0 0 6 0 1 0 0 ffff
  //   contents of rom_3 (hex, n*v repeats v):
  //   0 0 1
  //   contents of rom_4 (hex, n*v repeats v):
  //   0 0 6 8 6 1 0 8 6 1
endmodule

module CPU (
  input  [15:0] OPCode,
  input  [15:0] C1,
  input  [15:0] C2,
  input  [15:0] C3,
  input  [15:0] IP,
  input  Reset,
  output [15:0] OU,
  output Conditional,
  output [15:0] Display,
  output [15:0] Text
);

  wire and_2_out, and_3_out, and_4_out, and_5_out, clock_1_out, comparator_1_eq, comparator_1_gt,
       comparator_1_lt, controlled_buffer_1_out, controlled_buffer_2_out, controlled_buffer_3_out,
       controlled_buffer_4_out, controlled_buffer_5_out, controlled_buffer_6_out, controlled_buffer_7_out,
       controlled_buffer_8_out, controlled_buffer_9_out, controlled_buffer_10_out, controlled_buffer_12_out,
       controlled_buffer_13_out, controlled_buffer_14_out, controlled_buffer_15_out,
       controlled_buffer_16_out, controlled_buffer_17_out, controlled_buffer_19_out, cpudecider_1_add,
       cpudecider_1_addi, cpudecider_1_amd, cpudecider_1_ieq, cpudecider_1_ieqi, cpudecider_1_igt,
       cpudecider_1_igti, cpudecider_1_ilt, cpudecider_1_ilti, cpudecider_1_imm, cpudecider_1_ineq,
       cpudecider_1_ineqi, cpudecider_1_jmp, cpudecider_1_namd, cpudecider_1_nom, cpudecider_1_nut,
       cpudecider_1_om, cpudecider_1_res, cpudecider_1_shl, cpudecider_1_shr, cpudecider_1_sub,
       cpudecider_1_subi, cpudecider_1_xnom, cpudecider_1_xom, demultiplexer_1_out0, demultiplexer_1_out1,
       demultiplexer_1_out2, demultiplexer_1_out3, demultiplexer_1_out4, demultiplexer_1_out5,
       demultiplexer_1_out6, demultiplexer_1_out7, demultiplexer_1_out8, demultiplexer_1_out9,
       demultiplexer_2_out0, demultiplexer_2_out1, demultiplexer_2_out2, demultiplexer_2_out3,
       demultiplexer_2_out4, demultiplexer_2_out5, demultiplexer_2_out6, demultiplexer_3_out0,
       demultiplexer_3_out1, demultiplexer_3_out2, demultiplexer_3_out3, demultiplexer_3_out4,
       demultiplexer_3_out5, demultiplexer_3_out6, demultiplexer_3_out7, demultiplexer_4_out0,
       demultiplexer_4_out1, demultiplexer_4_out2, demultiplexer_4_out3, demultiplexer_4_out4,
       demultiplexer_4_out5, demultiplexer_4_out6, demultiplexer_4_out7, MOV, not_1_out, not_3_out, or_1_out,
       or_2_out, or_3_out, or_4_out, or_5_out, or_6_out, or_7_out, or_8_out, or_9_out, or_10_out, or_11_out,
       or_13_out, or_14_out, or_15_out, or_16_out, or_17_out, or_18_out, or_20_out, POP, PSH, undriven;
  wire [15:0] adder_1_out, and_1_out, controlled_buffer_11_out, controlled_buffer_18_out,
       controlled_buffer_20_out, controlled_buffer_21_out, controlled_buffer_29_out,
       controlled_buffer_30_out, controlled_buffer_43_out, nand_1_out, nor_1_out, not_2_out, or_12_out,
       register_1_q, register_2_q, register_3_q, register_4_q, register_5_q, register_6_q, register_7_q,
       shifter_1_out, shifter_2_out, stack_1_out_4, subtractor_1_out, xnor_1_out, xor_1_out;

  CPUDecider cpudecider_1 (
    .in_1(OPCode), .MOV(MOV), .IMM(cpudecider_1_imm), .PSH(PSH), .POP(POP), .RES(cpudecider_1_res),
    .ADD(cpudecider_1_add), .SUB(cpudecider_1_sub), .AMD(cpudecider_1_amd), .OM(cpudecider_1_om),
    .NAMD(cpudecider_1_namd), .NOM(cpudecider_1_nom), .XOM(cpudecider_1_xom), .XNOM(cpudecider_1_xnom),
    .NUT(cpudecider_1_nut), .SHR(cpudecider_1_shr), .SHL(cpudecider_1_shl), .IGT(cpudecider_1_igt),
    .IEQ(cpudecider_1_ieq), .INEQ(cpudecider_1_ineq), .ILT(cpudecider_1_ilt), .ADDi(cpudecider_1_addi),
    .SUBi(cpudecider_1_subi), .IGTi(cpudecider_1_igti), .IEQi(cpudecider_1_ieqi), .INEQi(cpudecider_1_ineqi),
    .ILTi(cpudecider_1_ilti), .JMP(cpudecider_1_jmp));  // open: NOOP, WriteRam, ReadRam
  Clock #(.phaseOffset(1)) clock_1 (.out(clock_1_out));
  Demultiplexer #(.select(4), .tristate("true")) demultiplexer_1 (
    .out0(demultiplexer_1_out0), .out1(demultiplexer_1_out1), .out2(demultiplexer_1_out2),
    .out3(demultiplexer_1_out3), .out4(demultiplexer_1_out4), .out5(demultiplexer_1_out5),
    .out6(demultiplexer_1_out6), .out7(demultiplexer_1_out7), .out8(demultiplexer_1_out8),
    .out9(demultiplexer_1_out9), .in(clock_1_out), .sel(C3[3:0]));  // open: out10, out11, out12, out13, out14, out15
  Demultiplexer #(.select(4), .tristate("true")) demultiplexer_2 (
    .out0(demultiplexer_2_out0), .out1(demultiplexer_2_out1), .out2(demultiplexer_2_out2),
    .out3(demultiplexer_2_out3), .out4(demultiplexer_2_out4), .out5(demultiplexer_2_out5),
    .out6(demultiplexer_2_out6), .in(1'b1), .sel(C1[3:0]));  // open: out7, out8, out9, out10, out11, out12, out13, out14, out15
  assign controlled_buffer_1_out = cpudecider_1_res ? demultiplexer_2_out0 : 1'bz;  // Controlled_Buffer controlled_buffer_1
  assign controlled_buffer_2_out = cpudecider_1_res ? demultiplexer_2_out1 : 1'bz;  // Controlled_Buffer controlled_buffer_2
  or or_1 (or_1_out, MOV, cpudecider_1_imm, POP, cpudecider_1_add, cpudecider_1_sub, cpudecider_1_amd, cpudecider_1_om, cpudecider_1_namd, cpudecider_1_nom, cpudecider_1_xom, cpudecider_1_xnom, cpudecider_1_nut, cpudecider_1_shr, cpudecider_1_shl, cpudecider_1_addi, cpudecider_1_subi);
  assign controlled_buffer_3_out = cpudecider_1_res ? demultiplexer_2_out2 : 1'bz;  // Controlled_Buffer controlled_buffer_3
  assign controlled_buffer_4_out = cpudecider_1_res ? demultiplexer_2_out3 : 1'bz;  // Controlled_Buffer controlled_buffer_4
  assign controlled_buffer_5_out = cpudecider_1_res ? demultiplexer_2_out4 : 1'bz;  // Controlled_Buffer controlled_buffer_5
  assign controlled_buffer_6_out = cpudecider_1_res ? demultiplexer_2_out5 : 1'bz;  // Controlled_Buffer controlled_buffer_6
  assign controlled_buffer_7_out = or_1_out ? demultiplexer_1_out0 : 1'bz;  // Controlled_Buffer controlled_buffer_7
  assign controlled_buffer_8_out = or_1_out ? demultiplexer_1_out1 : 1'bz;  // Controlled_Buffer controlled_buffer_8
  assign controlled_buffer_9_out = or_1_out ? demultiplexer_1_out2 : 1'bz;  // Controlled_Buffer controlled_buffer_9
  assign controlled_buffer_10_out = cpudecider_1_res ? demultiplexer_2_out6 : 1'bz;  // Controlled_Buffer controlled_buffer_10
  assign controlled_buffer_11_out = cpudecider_1_imm ? C1 : 16'bz;  // Controlled_Buffer controlled_buffer_11
  assign controlled_buffer_12_out = or_1_out ? demultiplexer_1_out3 : 1'bz;  // Controlled_Buffer controlled_buffer_12
  assign controlled_buffer_13_out = or_1_out ? demultiplexer_1_out4 : 1'bz;  // Controlled_Buffer controlled_buffer_13
  assign controlled_buffer_14_out = or_1_out ? demultiplexer_1_out5 : 1'bz;  // Controlled_Buffer controlled_buffer_14
  assign controlled_buffer_15_out = or_1_out ? demultiplexer_1_out6 : 1'bz;  // Controlled_Buffer controlled_buffer_15
  assign controlled_buffer_16_out = or_1_out ? demultiplexer_1_out8 : 1'bz;  // Controlled_Buffer controlled_buffer_16
  assign controlled_buffer_17_out = or_1_out ? demultiplexer_1_out9 : 1'bz;  // Controlled_Buffer controlled_buffer_17
  or or_2 (or_2_out, cpudecider_1_nom, cpudecider_1_add, cpudecider_1_sub, cpudecider_1_amd, cpudecider_1_om, cpudecider_1_namd, cpudecider_1_xom, cpudecider_1_xnom, cpudecider_1_igt, cpudecider_1_ieq, cpudecider_1_ilt, cpudecider_1_ineq);
  assign controlled_buffer_18_out = or_2_out ? C2 : 16'bz;  // Controlled_Buffer controlled_buffer_18
  assign controlled_buffer_19_out = or_1_out ? demultiplexer_1_out7 : 1'bz;  // Controlled_Buffer controlled_buffer_19
  assign controlled_buffer_20_out = or_10_out ? C1 : 16'bz;  // Controlled_Buffer controlled_buffer_20
  Register #(.width(16)) register_1 (
    .D(controlled_buffer_11_out), .clk(controlled_buffer_7_out), .Q(register_1_q), .clr(or_3_out));  // open: en
  Register #(.width(16)) register_2 (
    .D(controlled_buffer_11_out), .clk(controlled_buffer_8_out), .Q(register_2_q), .clr(or_4_out));  // open: en
  Register #(.width(16)) register_3 (
    .D(controlled_buffer_11_out), .clk(controlled_buffer_9_out), .Q(register_3_q), .clr(or_5_out));  // open: en
  Register #(.width(16)) register_4 (
    .D(controlled_buffer_11_out), .en(undriven), .clk(controlled_buffer_12_out), .Q(register_4_q),
    .clr(or_6_out));
  Register #(.width(16)) register_5 (
    .D(controlled_buffer_11_out), .en(undriven), .clk(controlled_buffer_13_out), .Q(register_5_q),
    .clr(or_7_out));
  Register #(.width(16)) register_6 (
    .D(controlled_buffer_11_out), .en(undriven), .clk(controlled_buffer_14_out), .Q(register_6_q),
    .clr(or_8_out));
  Register #(.width(16)) register_7 (
    .D(controlled_buffer_11_out), .en(undriven), .clk(controlled_buffer_15_out), .Q(register_7_q),
    .clr(or_9_out));
  Demultiplexer #(.select(4)) demultiplexer_3 (
    .out0(demultiplexer_3_out0), .out1(demultiplexer_3_out1), .out2(demultiplexer_3_out2),
    .out3(demultiplexer_3_out3), .out4(demultiplexer_3_out4), .out5(demultiplexer_3_out5),
    .out6(demultiplexer_3_out6), .out7(demultiplexer_3_out7), .in(1'b1), .sel(controlled_buffer_20_out[3:0]));  // open: out8, out9, out10, out11, out12, out13, out14, out15
  or or_3 (or_3_out, controlled_buffer_1_out, Reset);
  or or_4 (or_4_out, controlled_buffer_2_out, Reset);
  or or_5 (or_5_out, controlled_buffer_3_out, Reset);
  or or_6 (or_6_out, controlled_buffer_4_out, Reset);
  or or_7 (or_7_out, controlled_buffer_5_out, Reset);
  or or_8 (or_8_out, controlled_buffer_6_out, Reset);
  or or_9 (or_9_out, controlled_buffer_10_out, Reset);
  assign controlled_buffer_21_out = demultiplexer_3_out7 ? IP : 16'bz;  // Controlled_Buffer controlled_buffer_21
  or or_10 (or_10_out, cpudecider_1_xom, cpudecider_1_igti, cpudecider_1_addi, MOV, PSH, cpudecider_1_add, cpudecider_1_sub, cpudecider_1_amd, cpudecider_1_om, cpudecider_1_namd, cpudecider_1_nom, cpudecider_1_ineqi, cpudecider_1_xnom, cpudecider_1_nut, cpudecider_1_shr, cpudecider_1_shl, cpudecider_1_igt, cpudecider_1_ieq, cpudecider_1_ilt, cpudecider_1_subi, cpudecider_1_ieqi, cpudecider_1_ilti, cpudecider_1_ineq);
  assign controlled_buffer_21_out = demultiplexer_3_out3 ? register_4_q : 16'bz;  // Controlled_Buffer controlled_buffer_22
  assign controlled_buffer_21_out = demultiplexer_3_out4 ? register_5_q : 16'bz;  // Controlled_Buffer controlled_buffer_23
  assign controlled_buffer_21_out = demultiplexer_3_out5 ? register_6_q : 16'bz;  // Controlled_Buffer controlled_buffer_24
  assign controlled_buffer_21_out = demultiplexer_3_out6 ? register_7_q : 16'bz;  // Controlled_Buffer controlled_buffer_25
  assign controlled_buffer_21_out = demultiplexer_3_out0 ? register_1_q : 16'bz;  // Controlled_Buffer controlled_buffer_26
  assign controlled_buffer_21_out = demultiplexer_3_out1 ? register_2_q : 16'bz;  // Controlled_Buffer controlled_buffer_27
  assign controlled_buffer_21_out = demultiplexer_3_out2 ? register_3_q : 16'bz;  // Controlled_Buffer controlled_buffer_28
  Demultiplexer #(.select(4)) demultiplexer_4 (
    .out0(demultiplexer_4_out0), .out1(demultiplexer_4_out1), .out2(demultiplexer_4_out2),
    .out3(demultiplexer_4_out3), .out4(demultiplexer_4_out4), .out5(demultiplexer_4_out5),
    .out6(demultiplexer_4_out6), .out7(demultiplexer_4_out7), .in(1'b1), .sel(controlled_buffer_18_out[3:0]));  // open: out8, out9, out10, out11, out12, out13, out14, out15
  assign controlled_buffer_29_out = demultiplexer_4_out7 ? IP : 16'bz;  // Controlled_Buffer controlled_buffer_29
  assign controlled_buffer_30_out = or_11_out ? C2 : 16'bz;  // Controlled_Buffer controlled_buffer_30
  assign controlled_buffer_29_out = demultiplexer_4_out3 ? register_4_q : 16'bz;  // Controlled_Buffer controlled_buffer_31
  assign controlled_buffer_29_out = demultiplexer_4_out4 ? register_5_q : 16'bz;  // Controlled_Buffer controlled_buffer_32
  assign controlled_buffer_29_out = demultiplexer_4_out5 ? register_6_q : 16'bz;  // Controlled_Buffer controlled_buffer_33
  assign controlled_buffer_29_out = demultiplexer_4_out6 ? register_7_q : 16'bz;  // Controlled_Buffer controlled_buffer_34
  assign controlled_buffer_29_out = demultiplexer_4_out0 ? register_1_q : 16'bz;  // Controlled_Buffer controlled_buffer_35
  assign controlled_buffer_29_out = demultiplexer_4_out1 ? register_2_q : 16'bz;  // Controlled_Buffer controlled_buffer_36
  assign controlled_buffer_29_out = demultiplexer_4_out2 ? register_3_q : 16'bz;  // Controlled_Buffer controlled_buffer_37
  or or_11 (or_11_out, cpudecider_1_addi, cpudecider_1_subi, cpudecider_1_igti, cpudecider_1_ieqi, cpudecider_1_ilti, cpudecider_1_ineqi);
  not not_1 (not_1_out, or_11_out);
  assign controlled_buffer_30_out = not_1_out ? controlled_buffer_29_out : 16'bz;  // Controlled_Buffer controlled_buffer_38
  assign controlled_buffer_11_out = MOV ? controlled_buffer_21_out : 16'bz;  // Controlled_Buffer controlled_buffer_39
  assign controlled_buffer_11_out = controlled_buffer_43_out;  // Buffer buffer_1, 16 bits wide
  Adder #(.width(16)) adder_1 (
    .a(controlled_buffer_21_out), .b(controlled_buffer_30_out), .out(adder_1_out));  // open: cin, cout
  Subtractor #(.width(16)) subtractor_1 (
    .a(controlled_buffer_21_out), .b(controlled_buffer_30_out), .out(subtractor_1_out));  // open: bin, bout
  assign and_1_out = controlled_buffer_21_out & controlled_buffer_30_out;  // AND_Gate and_1, 16 bits wide
  assign or_12_out = controlled_buffer_21_out | controlled_buffer_30_out;  // OR_Gate or_12, 16 bits wide
  assign nand_1_out = ~(controlled_buffer_21_out & controlled_buffer_30_out);  // NAND_Gate nand_1, 16 bits wide
  assign nor_1_out = ~(controlled_buffer_21_out | controlled_buffer_30_out);  // NOR_Gate nor_1, 16 bits wide
  assign xor_1_out = controlled_buffer_21_out ^ controlled_buffer_30_out;  // XOR_Gate xor_1, 16 bits wide
  assign not_2_out = ~controlled_buffer_21_out;  // NOT_Gate not_2, 16 bits wide
  Shifter #(.shift("lr"), .width(16)) shifter_1 (.in(controlled_buffer_21_out), .\dist (4'b0001), .out(shifter_1_out));
  Shifter #(.width(16)) shifter_2 (.in(controlled_buffer_21_out), .\dist (4'b0001), .out(shifter_2_out));
  Comparator #(.mode("unsigned"), .width(16)) comparator_1 (
    .a(controlled_buffer_21_out), .b(controlled_buffer_30_out), .gt(comparator_1_gt), .eq(comparator_1_eq),
    .lt(comparator_1_lt));
  assign OU = controlled_buffer_19_out ? controlled_buffer_11_out : 16'bz;  // Controlled_Buffer controlled_buffer_40
  assign Display = controlled_buffer_16_out ? controlled_buffer_11_out : 16'bz;  // Controlled_Buffer controlled_buffer_41
  assign Text = controlled_buffer_17_out ? controlled_buffer_11_out : 16'bz;  // Controlled_Buffer controlled_buffer_42
  or or_13 (or_13_out, cpudecider_1_add, cpudecider_1_addi);
  assign controlled_buffer_43_out = or_13_out ? adder_1_out : 16'bz;  // Controlled_Buffer controlled_buffer_43
  or or_14 (or_14_out, cpudecider_1_sub, cpudecider_1_subi);
  assign controlled_buffer_43_out = or_14_out ? subtractor_1_out : 16'bz;  // Controlled_Buffer controlled_buffer_44
  assign controlled_buffer_43_out = cpudecider_1_amd ? and_1_out : 16'bz;  // Controlled_Buffer controlled_buffer_45
  assign controlled_buffer_43_out = cpudecider_1_om ? or_12_out : 16'bz;  // Controlled_Buffer controlled_buffer_46
  assign xnor_1_out = ~(controlled_buffer_21_out ^ controlled_buffer_30_out);  // XNOR_Gate xnor_1, 16 bits wide
  or or_15 (or_15_out, POP, PSH);
  Stack stack_1 (.POP(POP), .PUSH(PSH), .IP(controlled_buffer_21_out), .out_4(stack_1_out_4));
  assign controlled_buffer_43_out = or_15_out ? stack_1_out_4 : 16'bz;  // Controlled_Buffer controlled_buffer_47
  assign controlled_buffer_43_out = cpudecider_1_namd ? nand_1_out : 16'bz;  // Controlled_Buffer controlled_buffer_48
  assign controlled_buffer_43_out = cpudecider_1_nom ? nor_1_out : 16'bz;  // Controlled_Buffer controlled_buffer_49
  assign controlled_buffer_43_out = cpudecider_1_xom ? xor_1_out : 16'bz;  // Controlled_Buffer controlled_buffer_50
  assign controlled_buffer_43_out = cpudecider_1_xnom ? xnor_1_out : 16'bz;  // Controlled_Buffer controlled_buffer_51
  and and_2 (and_2_out, comparator_1_lt, or_16_out);
  assign controlled_buffer_43_out = cpudecider_1_nut ? not_2_out : 16'bz;  // Controlled_Buffer controlled_buffer_52
  assign controlled_buffer_43_out = cpudecider_1_shr ? shifter_1_out : 16'bz;  // Controlled_Buffer controlled_buffer_53
  assign controlled_buffer_43_out = cpudecider_1_shl ? shifter_2_out : 16'bz;  // Controlled_Buffer controlled_buffer_54
  or or_16 (or_16_out, cpudecider_1_igti, cpudecider_1_ilt);
  or or_17 (or_17_out, cpudecider_1_ieqi, cpudecider_1_ieq);
  or or_18 (or_18_out, cpudecider_1_igt, cpudecider_1_ilti);
  and and_3 (and_3_out, comparator_1_gt, or_18_out);
  not not_3 (not_3_out, comparator_1_eq);
  and and_4 (and_4_out, comparator_1_eq, or_17_out);
  or or_19 (Conditional, and_2_out, and_4_out, cpudecider_1_jmp, and_3_out, and_5_out);
  or or_20 (or_20_out, cpudecider_1_ineqi, cpudecider_1_ineq);
  and and_5 (and_5_out, not_3_out, or_20_out);
endmodule

module Stack (
  input  POP,
  input  PUSH,
  input  [15:0] IP,
  output [15:0] out_4
);

  wire and_1_out, and_2_out, buffer_1_out, buffer_2_out, buffer_3_out, buffer_4_out, buffer_5_out,
       buffer_6_out, buffer_7_out, buffer_8_out, not_1_out, not_2_out, or_1_out;
  wire [15:0] counter_1_q;

  buf buffer_1 (buffer_1_out, PUSH);
  buf buffer_2 (buffer_2_out, buffer_1_out);
  not not_1 (not_1_out, buffer_2_out);
  not not_2 (not_2_out, POP);
  and and_1 (and_1_out, not_2_out, POP);
  and and_2 (and_2_out, not_1_out, buffer_2_out);
  Counter #(.max('hffff), .width(16)) counter_1 (
    .up(buffer_3_out), .clk(or_1_out), .Q(counter_1_q));  // open: clr, load, count, D, carry
  buf buffer_3 (buffer_3_out, and_2_out);
  or or_1 (or_1_out, and_1_out, and_2_out);
  buf buffer_4 (buffer_4_out, or_1_out);
  buf buffer_5 (buffer_5_out, buffer_4_out);
  buf buffer_6 (buffer_6_out, and_2_out);
  buf buffer_7 (buffer_7_out, buffer_6_out);
  buf buffer_8 (buffer_8_out, buffer_7_out);
  RAM #(.addrWidth(16), .asyncread("true"), .dataWidth(16)) ram_1 (
    .addr(counter_1_q), .we(buffer_8_out), .clk(buffer_5_out), .din(IP), .dout(out_4));  // open: oe
endmodule

module CPUDecider (
  input  [15:0] in_1,
  output NOOP,
  output MOV,
  output IMM,
  output PSH,
  output POP,
  output RES,
  output ADD,
  output SUB,
  output AMD,
  output OM,
  output NAMD,
  output NOM,
  output XOM,
  output XNOM,
  output NUT,
  output SHR,
  output SHL,
  output IGT,
  output IEQ,
  output INEQ,
  output ILT,
  output ADDi,
  output SUBi,
  output IGTi,
  output IEQi,
  output INEQi,
  output ILTi,
  output JMP,
  output WriteRam,
  output ReadRam
);

  wire demultiplexer_1_out30;

  Demultiplexer #(.select(5)) demultiplexer_1 (
    .out0(NOOP), .out1(MOV), .out2(IMM), .out3(PSH), .out4(POP), .out5(RES), .out6(ADD), .out7(SUB),
    .out8(AMD), .out9(OM), .out10(NAMD), .out11(NOM), .out12(XOM), .out13(XNOM), .out14(NUT), .out15(SHR),
    .out16(SHL), .out17(IGT), .out18(IEQ), .out19(INEQ), .out20(ILT), .out21(ADDi), .out22(SUBi),
    .out23(IGTi), .out24(IEQi), .out25(INEQi), .out26(ILTi), .out27(JMP), .out28(WriteRam), .out29(ReadRam),
    .out30(demultiplexer_1_out30), .in(1'b1), .sel(in_1[4:0]));  // open: out31
endmodule

module GPU (
  input  Reset,
  input  Clock,
  input  [15:0] Color,
  output ClockOU,
  output [4:0] X,
  output [4:0] Y,
  output [15:0] Colorr
);

  wire counter_1_carry, not_1_out, or_1_out;

  not not_1 (not_1_out, Color[0]);
  or or_1 (or_1_out, not_1_out, Color[1], Color[2], Color[3], Color[4], Color[5], Color[6], Color[7], Color[8], Color[9], Color[10], Color[11], Color[12], Color[13], Color[14], Color[15]);
  assign ClockOU = or_1_out ? Clock : 1'bz;  // Controlled_Buffer controlled_buffer_1
  Counter #(.max('h1f), .width(5)) counter_1 (
    .clr(Reset), .up(1'b1), .clk(ClockOU), .carry(counter_1_carry), .Q(X));  // open: load, count, D
  Counter #(.max('h1f), .trigger("falling"), .width(5)) counter_2 (
    .clr(Reset), .clk(counter_1_carry), .Q(Y));  // open: load, up, count, D, carry

  assign Colorr = Color;
endmodule

module TPU (
  input  [15:0] Char,
  input  Clock,
  output [6:0] out_3,
  output ClockOU
);

  wire not_1_out, or_1_out;

  not not_1 (not_1_out, Char[0]);
  or or_1 (or_1_out, not_1_out, Char[1], Char[2], Char[3], Char[4], Char[5], Char[6], Char[7], Char[8], Char[9], Char[10], Char[11], Char[12], Char[13], Char[14], Char[15]);
  assign ClockOU = or_1_out ? Clock : 1'bz;  // Controlled_Buffer controlled_buffer_1

  assign out_3 = Char[6:0];
endmodule

module orrer (
  input  [15:0] in_1,
  output out_2
);

  wire not_1_out;

  not not_1 (not_1_out, in_1[0]);
  or or_1 (out_2, not_1_out, in_1[1], in_1[2], in_1[3], in_1[4], in_1[5], in_1[6], in_1[7], in_1[8], in_1[9], in_1[10], in_1[11], in_1[12], in_1[13], in_1[14], in_1[15]);
endmodule
